# Fritzing sketch RC_Transmitter (saved by Fritzing 0.6.2b)
breadboards: 1

parts:
  U1 = 3-Axis Accelerometer Breakout [part_number="ADXL 330"]
  Arduino1 = Arduino Nano v2.3
  U2 = mystery part, 4 pins [chip_label="TX unit" spacing=300mil part_number="433 MHz transmitter"]
  S1 = Toggle Switch [package=THT]
  ANT1 = Antenna
  C1 = Electrolytic Capacitor [capacitance=200µF voltage=16V package="100 mil [THT, electrolytic]"]
  R1 = Resistor [tolerance=±5% resistance=220 package=THT]
  LED1 = Red LED - 5mm [package="5 mm [THT]"]
  R2 = Resistor [tolerance=±5% resistance=220 package=THT]
  LED2 = Red LED - 5mm [package="5 mm [THT]"]
  R3 = Resistor [tolerance=±5% resistance=220 package=THT]
  LED3 = Red LED - 5mm [package="5 mm [THT]"]
  VCC1 = Battery block 9V
  R4 = Resistor [tolerance=±5% resistance=220 package=THT]
  LED4 = Red LED - 5mm [package="5 mm [THT]"]
  R5 = Resistor [tolerance=±5% resistance=220 package=THT]
  R6 = Resistor [tolerance=±5% resistance=220 package=THT]
  R7 = Resistor [tolerance=±5% resistance=220 package=THT]
  R8 = Resistor [tolerance=±5% resistance=220 package=THT]
  LED5 = Red LED - 5mm [package="5 mm [THT]"]
  LED6 = Red LED - 5mm [package="5 mm [THT]"]
  LED7 = Red LED - 5mm [package="5 mm [THT]"]
  LED8 = Red LED - 5mm [package="5 mm [THT]"]
  S2 = Pushbutton [part_number="backward btn" package="[THT]"]
  S3 = Pushbutton [part_number="beep btn" package="[THT]"]
  S4 = Pushbutton [part_number="forward btn" package="[THT]"]

nets (from the schematic view):
  N1: U1.Z, Arduino1.A2
  N2: U1.Y, Arduino1.A6
  N3: U1.X, Arduino1.A7
  GND: U1.GND, Arduino1.GND, U2.pin4, C1.-, LED1.cathode, LED2.cathode, LED3.cathode, VCC1.-, LED4.cathode, LED5.cathode, LED6.cathode, LED7.cathode, LED8.cathode, S2.Pin_1, S3.Pin_1, S3.Pin_2, S4.Pin_1
  VDD: U1.VDD, Arduino1.+5V, U2.pin2
  N4: Arduino1.D2, S3.Pin_3, S3.Pin_4
  N5: Arduino1.D3, S2.Pin_3, S2.Pin_4
  N6: Arduino1.D4, R1.Pin_1
  N7: Arduino1.D5, R2.Pin_1
  N8: Arduino1.D6, R3.Pin_1
  N9: Arduino1.D8, R4.Pin_1
  N10: Arduino1.D9, R8.Pin_1
  N11: Arduino1.D10, R7.Pin_1
  N12: Arduino1.D11, R5.Pin_1
  N13: Arduino1.D12, R6.Pin_1
  N14: Arduino1.D13, U2.pin3
  N15: Arduino1.A0, S4.Pin_3
  N16: Arduino1.VIN, S1.COM, C1.+
  N17: U2.pin1, ANT1.antenna_lead
  N18: S1.L2, VCC1.+
  N19: R1.Pin_0, LED1.anode
  N20: R2.Pin_0, LED2.anode
  N21: R3.Pin_0, LED3.anode
  N22: R4.Pin_0, LED4.anode
  N23: R5.Pin_0, LED5.anode
  N24: R6.Pin_0, LED6.anode
  N25: R8.Pin_0, LED8.anode
